# Fritzing sketch Water_DirectWiFi (saved by Fritzing 0.9.3b)
circuit board: 7cm x 3cm

parts:
  D1 = SOLAR-IXYS [part_number="Solar 5V, 3W" package=solarbit-12x1]
  Part7 = Power Cell LiPo Charger/Booster [part_number=TP4056]
  R1 = Resistor [tolerance=±5% resistance=680k package=THT]
  R2 = Resistor [tolerance=±5% resistance=680k package=THT]
  C1 = Ceramic Capacitor [capacitance=100nF package="100 mil [THT, multilayer]"]
  Part8 = Arduino Pro Mini v13
  BAT1 = Battery Holders [part_number="18650, 3400mAh" package=battery-aa]
  Rain_Senor = Reed switch [part_number="Rain Gauge" package=THT]
  Part10 = Adafruit SHT31-D Sensirion Temperature/Humidity Sensor [part_number="Adafruit #2857"]
  U3 = ESP8266 WiFi Module [part_number=ESP8266]
  C3 = Electrolytic Capacitor [capacitance=10µF package="100 mil [THT, electrolytic]"]
  U4 = LM3480IM4 [part_number=5v package=sot23-3]
  X1 = USB Connectors [part_number=3G-USB-Dongle package=usb-a-s-nosilk-female]
  Q2 = Basic FET N-Channel [part_number=AO3400A package="TO220 [THT]"]
  R3 = Resistor [tolerance=±5% resistance=100 package=THT]
  R4 = Resistor [tolerance=±5% resistance=300k package=THT]
  U2 = LM3480IM4 [part_number=3.3v package=sot23-3]
  R5 = Resistor [tolerance=±5% resistance=300k package=THT]
  R6 = Resistor [tolerance=±5% resistance=100 package=THT]  # not connected
  Q3 = Basic FET N-Channel [part_number=AO3400A package="TO220 [THT]"]
  X2 = USB Connectors [part_number=5V-Analog-Sensor package=usb-a-s-nosilk-female]  # not connected
  J1 = male pin header, 2 pins [form="♂ (male)" part_number="3G/WiFi mode"]
  HC-SR1 = HC-SR04

nets (from the breadboard view):
  N1: D1.A, Part7.5VIN
  GND: D1.C, Part7.GND, R2.Pin_1, C1.1, Part8.GND, BAT1.-, Rain_Senor.pin_1, U2.GND, J1.pin2
  N2: Part7.VBATT, BAT1.+
  N3: R1.Pin_0, Part8.RAW
  N4: R1.Pin_1, R2.Pin_0, C1.0, Part8.A2
  N5: Part8.A4, Part10.SDA
  N6: Part8.A5, Part10.SCL
  VCC: Part8.VCC, Part10.VIN, HC-SR1.VCC
  N7: Part8.D9_PWM, U3.CH_PD
  N8: Part8.D8, U3.RXD
  N9: Part8.D7, U3.TXD
  N10: Part8.D6_PWM, J1.pin1
  N11: Part8.D4, HC-SR1.Echo
  N12: Part8.D3_PWM, HC-SR1.Trig
  N13: Part8.D2, Rain_Senor.pin_2
  GND_2: Part10.GND, U3.GND, C3.-, U4.GND, X1.GND, HC-SR1.GND
  N14: U3.VCC, U3.RST, C3.+, U2.OUT
  N15: U4.OUT, X1.VBUS
  N16: U4.IN, U2.IN
  N17: Q2.gate, R3.Pin_1
  N18: Q2.drain, R4.Pin_1
  N19: R5.Pin_0, Q3.gate
  N20: R5.Pin_1, Q3.source

notes:
  Solar Panel 6V 3W
  18650,3400mAh
  2 x 680k
  0.1uF

custom parts:
  Adafruit SHT31-D Sensirion Temperature/Humidity Sensor: Sensirion Temperature/Humidity sensors are some of the finest & highest-accuracy devices you can get. And, finally we have some that have a true I2C interface for easy reading. The SHT31-D sensor has an excellent ±2% relative humidity and ±0.3°C accuracy for most uses. Unlike earlier SHT sensors, this sensor has a true I2C interface, and (bonus!) even with two address options. It also is 3V or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
  ESP8266 WiFi Module: Generic WiFi Module based on the ESP8266 with onboard PCB antenna and UART communications
  HC-SR04: This is a HC-SR04 Ultrasonic Distance Sensor

// code stored in the sketch: BER_Function.ino
uint8_t getBER(void) {            // Calculate Error rate (BER)
    uint8_t errCount = NumberOfSetBits(DataErr[0]) + NumberOfSetBits(DataErr[1]) + NumberOfSetBits(DataErr[2]) + NumberOfSetBits(DataErr[3]);
    return (uint8_t)((float)errCount/1.28);
}

void updateBER(boolean SendSuccess) {   // Update BER array of send result of the SQN
    uint32_t errorBitMask;
    uint8_t errorByteCount = (((SQN - 1)/32) % 4);   // errorByteCounter = 0..3 for every 32 bits

    errorBitMask = 0x00000001;
    //errorBitMask = errorBitMask << (SQN - (errorByteCount * 32) - 1);       //Shift left sequenceNumber - 1 bit (0..31)
    errorBitMask = errorBitMask << ((SQN - 1) % 32);                          //Shift left sequenceNumber - 1 bit (0..31)
    if (SendSuccess) {
        DataErr[errorByteCount] &= ~errorBitMask;               // Clear error bit
    } else {    // sent failed
        DataErr[errorByteCount] |= errorBitMask;                // Set error bit
    }
}

uint8_t NumberOfSetBits(uint32_t i) {   // Count numnber of bit 1
     i = i - ((i >> 1) & 0x55555555);
     i = (i & 0x33333333) + ((i >> 2) & 0x33333333);
     return (((i + (i >> 4)) & 0x0F0F0F0F) * 0x01010101) >> 24;
}

// code stored in the sketch: Fritzing_Readme.ino
:Author: tbdltee
:Email: tbdltee@gmail.com
:Date: 06-Dec-2017
:Revision: C
:License: Public Domain
:Patent Pending (Reg.1701003801)

=== Revision History

1.0	- first release
1.1	- fixed data not update to Gsheet if web monitor not launch
	- wifi LED blink on web activitiy.
	- Tx/Rx station send distance in cm instead of mm
	- fixed ackPayload inconsistance received.
	- DBserver_Module.ino change to Web_Module.ino
2.0	- support weather information
	- support remote batt level (bvxxx), Tx interval (ivxxx) and weather counter setting (iwxxx)
	- support debug information
	- SR04 distance data with measurement quality.
	- ESP8266: static web content use PROGMEM to improve stability
	- ESP8266 auto-restart if OTA failed.
	- wifi LED: fast blink during OTA, slow blink during wifi config
	- re-code serial monitor of Arduino and ESP8266 to improve Arduino-ESP8266 communication
	- code clean up
2.1	- Remote Battery calibration setting received value bv321..bv420 for actual volt of 3.21V..4.20V
	- Increase Counter limitation from 65,535 to 655,359,999
	- add ESP watchdog interval 30 sec
	- Add counter to monitor ESP init.
	- hPA display fixed.
2.2	- Remove hPA measurement report and change to Rain Volume information
	- Remove Weather Counter Inverval configuration. Weather info always send every 1 min.
	- Allow only 1 session of Web monitoring.
	- DB internet (GSheet) update interval change from 1 min to 3 min.
	- Tx Data received interval gap (to reset info to zero) change from 110% to 220%
3.0	- Remove Watchdog module due to bug in bootloader of Arduino Pro Mini and change to program restart.
	- Sent Battery info to Gsheet dashboard
	- Re-Init RF24 if no data received from all Tx Stations for 2 min.
	- Restart ESP if WiFi-config-mode timeout + too many retries of Update_LogDB (no more grace period) to be able to re-connect to WiFi
3.1	- Send last received data instead of current data to internet.
	- Show software version in Debug page
4.0	- Increase RF24 radio listening pipe from 5 to 6 pipes
	- Radio pipe 0..3 for Water level Tx Station. 1 station support weather info
	- Radio pipe 4..5 for Ambiant Tx Station (multiple ambiant sensors per stations)
	- RF24 support max 3 AckPayload FIFO. Replace with AckPayload buffer, 2 ackPayload per Tx station. Result in 1 Tx delay of CMD in ackPayload
	- Change STS counter from uint16_t of 1x + 10x to uint32_t
	- Increase watchdog timer from 3sec to 30sec
4.1	- Support of changing Tx Station Name.
	- fixed ESP Rx buffer full if Internet activity take long time.
	- Improve debug information
4.2	- Arduino pause sending data during ESP sending data to internet to avoid ESP Rx buffer full.
	- Improve ESP-Arduino communication. (Shorten text)
	- Arduino Init by query ESP status instead of restart ESP.
	- Tx inverval is 5 sec and cannot configure.
4.3	- Station 4/5 can swap inside-outside TempC/RH value
	- Web request stop after 2 times failures with 'timeout' error
4.4	- Tx Station: add RF24reInit Counter. If too many RF24 re-init, restart node
	- Tx Station: re-init RF24 if too many Tx failure
	- Tx Station: Improve RF24 power control.
	- Rx Station: Use average top 3 of 5 (remove min-max) to send to internet
	- Rx Station: Show inernet status on web page
	- Rx Station: Improve Interent/Wifi re-connection handling
	- Rx Station: Support command "ClearStat" to reset counters
4.5 - Rx Station: improve RF24 hardware failure detected and re-init
	- Rx Station: send data to ESP every 1 sec to distribute communication load.
4.6 - Rx Station: ESP code re-compile with new ESP8266 library. Must compile with 1M(no SPIFFS)
	- Rx Station: Change AP config mode to SSID: iotConfigAP, PASS: iotconfig.
	- Rx Station: ESP, Add Serial data simulation module
	- Rx Station: add 500uS delay on Serial read to improve Serial port stability. (1 000 000uS x 8/19200bps = 416uS/byte
	- Rx Station: Packing data in GET url to shorten data consumption.
	- Tx Station: Automatic update Batt Level to 100% if batt level calc more than 4.20v
	
=== Project: Wireless Water Level measurement

This project is using HC-SR04p ultrasonic to measure the water level and send the information to the receiver.
The receiver has built-in web server which user can see the water level in real-time. The data from all Tx station
 will be sent to Google Sheet for data logging.
The receiver can support max 6 Tx stations with th following measurement capablties:
	Station 1..4: Water Level, Outdoor weather information (Temp, RH and Rain Volume). Only lastest weather info will be display.
	Station 5..6: 2 (Inside/Outside) x Ambient information (Temp and RH)

=== About the code

How to measure Water Level:
- We do not measure the absolution water level. We measure the water level compare to the reference level. 
- The measuring distance equal to reference level is display as 0
- The measuring distance near than reference level is display as +level
- The measuring distance far than reference level is display as -level
- The formula to calculate the water level is
      Water level = Ref.Level - Measuring Distance

The code consists of 4 sketches:
- 1p1_Arduino_Tx1_4 	this is a code for Tx station 1..4 using Arduino Pro-Mini. Upload the code using USB-TTL adapter.
- 1p2_Arduino_Tx5_6 	this is a code for Tx station 5..6 using Arduino Pro-Mini. Upload the code using USB-TTL adapter.
- 2p1_Arduino_Rx     	this is a code for Rx_station using Arduino Pro-Mini. Upload the code using USB-TTL adapter.
- 2p2_ESP_GSheet_WEB  	this is a code for Rx_station using ESP8266. Upload the code via OTA. pass: iotmynock1

For Rx_station, Arduino Pro-Mini communicate to ESP8266 using Serial communication with pre-define set of commands. See more details
in the sketchs.
- max 6 Tx stations per Receiver.
	- Tx 1..4: Walter level and Outdoor weather information (Temp, RH, Rain)
	- Tx 5..6: Inside/Outside weather information (Temp, RH)
- Data recevied from each Tx station in every 5 sec.
- Ourdoor weather information received every 1 min.
- Data update to Google Sheet every 3 min.
- LED status:
    - RF24 led: flashing	- data received.
    - WiFi led: ON    		- ESP8266 init mode
				slow blink 	- AP config mode. Use device to connect SSID: SofAP, IP:192.198.4.1, user: admin, pass: admin123
                fast blink 	- OTA
				flashing	- data received.

=== How to use
Tx Station 1..4: the battery Voltage reader must be calibrated before use.
	- Set BattCalibrtion to 1, upload and run the sketch. The data should appear on the Rx_station.
	- Use multi-meter to measure battery level
	- Check the relevent Tx_station and put the command bvxxx, where xxx is volatagex100 read from voltemeter, e.g. 4.12V -> bv412
Rx Station:
	AP config mode:
		Use any device to connect SSID: SofAP, IP:192.198.4.1, user: admin, pass: admin123

	Normal Operation mode:
		Once connect to wifi, find the Receiver IP address and use web browser to access Water Monitoring Dashboard.
		To change setting, Select the station and type following command and press 'Set':
			- xxx: 			Set reference level
			- bvxxx:		Set Battery level, where xxx = 321..420 for battery level from voltmeter is 3.21V..4.20V
			- nvxxx:		Set Tx station name, where xxx is name of Tx station
			- cvSYSrestart: restart Rx Station
			- cvClearConfig:Clear Wifi config

=== Folder structure

....
 Sketch_WaterLevel        		=> Main Folder
  +-- 1p1_Arduino_Tx1_4       	=> Tx Station 1..4
	+-- 1p1_Arduino_Tx1_4.ino	=> Arduino main sketch
	+-- Peripheral_Function.ino => sketch contains peripherral functions, e.g. battery voltage reading, measuring distance
	+-- RF24_Tx_Module.ino      => sketch contains functions of RF24L01 handling
  	+-- Watchdog.ino     		=> sketch contains functions of watchdog and sleep module
  +-- 1p1_Arduino_Tx5_6       	=> Tx Station 5..6
	+-- 1p1_Arduino_Tx5_6.ino	=> Arduino main sketch
	+-- Peripheral_Function.ino => sketch contains peripherral functions, e.g. battery voltage reading, measuring distance
	+-- RF24_Tx_Module.ino      => sketch contains functions of RF24L01 handling
  	+-- Watchdog.ino     		=> sketch contains functions of watchdog and sleep module
  +-- 2p1_Arduino_Rx       		=> Rx Station, Arduino part sketch
	+-- 2p1_Arduino_Rx.ino   	=> Arduino main sketch
    +-- Node_Config.h    		=> Configuration file
    +-- RF24_Rx_Module.ino     	=> sketch contains functions of RF24L01 handling
  	+-- WiFi_Module.ino        	=> sketch contains functions to communicate with ESP8266
	+-- Watchdog.ino     		=> sketch contains functions of watchdog and sleep module
  +-- 2p2_ESP_GSheet_WEB		=> Rx Station, ESP8266 part sketch
	+-- 2p2_ESP_GSheet_WEB.ino  => ESP8266 main sketch
	+-- iNET_Module.ino  		=> sketch contains functions of Google Sheet and internet communication
	+-- mainWebPage.h  			=> sketch contains template of Webpage using for local web server
    +-- Node_Config.h    		=> Configuration file
	+-- SerialMon_Module.ino    => sketch contains functions of Serial communication with Arduino.
	+-- Web_Module.ino      	=> sketch contains functions of wifi handling and local web server
....

=== BOM
Rx Station:
| ID | Description                             	| Quantity
|  1 | Arduino Pro-Mini 3.3v 8MHz              	| 1
|  2 | ESP8266-01                              	| 1
|  3 | RF24L01p+PA+LNA                          | 1
|  4 | Micro USB breakout board                	| 1
|  5 | Capacitor 10uF                          	| 2
|  6 | Resistor 10kOhm                         	| 2
|  7 | blue LED (wifi status)                  	| 1
|  8 | red LED (RF24 data received status)     	| 1
|  9 | LM1117T-3.3v 800mA                      	| 1
| 10 | micro USB charging cable                	| 1
| 11 | USB charger, 500mA                      	| 1

Tx Station 1..4:
| ID | Description                             	| Quantity
|  1 | Arduino Pro-Mini 3.3v 8MHz              	| 1
|  2 | RF24L01p+PA+LNA                          | 1
|  3 | HC-SR04p				                 	| 1
|  4 | SHT31-D (Option)		                 	| 1
|  5 | Rain Gauge Sensor (Option)              	| 1
|  6 | Capacitor 10uF                          	| 1
|  7 | Capacitor 0.1uF                         	| 1
|  8 | Resistor 680kOhm							| 2
|  9 | Battery 18650, 3400mAh - no PCB         	| 1
| 10 | 18650 Battery Holder						| 1
| 11 | XC6206P332PR 800mA                      	| 1
| 12 | TP4056 LiPo charger with protection		| 1
| 13 | Diode 1N4001				                | 1
| 14 | Solar Panel 3W, 5.85v                   	| 1
| 15 | PVC straight joint 4"                   	| 1
| 16 | Water proof box, 70x120x50mm            	| 1

Tx Station 5..6:
| ID | Description                             	| Quantity
|  1 | Arduino Pro-Mini 3.3v 8MHz              	| 1
|  2 | RF24L01p+PA+LNA                          | 1
|  3 | BME280				                 	| 1
|  4 | SHT31-D									| 1
|  5 | Capacitor 10uF                          	| 1
|  6 | XC6206P332PR 800mA                      	| 1
|  7 | Water proof box, 2"x4"            		| 1

// code stored in the sketch: Peripheral_Function.ino
void Init_Peripheral() {
    // Set Ardiono for Initial SR04 configuration
    pinMode(SR04_TRIGpin, OUTPUT);
    digitalWrite(SR04_TRIGpin, LOW);
    pinMode(SR04_ECHOpin, INPUT);

    // Set Ardiono pin for LED bar
    for (uint8_t i = 0; i < 5; i++) {
        pinMode (LEDpin[i], OUTPUT);
        digitalWrite(LEDpin[i], LOW);
    }
}

void LEDBar(uint8_t LEDLevel) {             // LED Bar Level: 0..4
    for (uint8_t i = 0; i < 5; i++) {
        if (i < LEDLevel) {
            digitalWrite(LEDpin[i], HIGH);
        } else {
            digitalWrite(LEDpin[i], LOW);
        }
    }
}

uint16_t getDistance() {    // Get distance (mm) from SR04 configuration
    uint32_t pulse_width;    
    digitalWrite(SR04_TRIGpin, HIGH);   // Hold the trigger pin high for at least 10 us
    delayMicroseconds(10);
    digitalWrite(SR04_TRIGpin, LOW);
    pulse_width = pulseIn(SR04_ECHOpin, HIGH, MAX_DIST);   //Returns the pulse width in uS or 0 if no complete pulse was received within the timeout.
    return (uint16_t)((float)pulse_width / 5.82);  // return distance, mm
}

// code stored in the sketch: RF24_Tx.ino
#include <SPI.h>
#include <RF24.h>
#include <SimpleTimer.h>

// =============== Configurable Data ===================
// Timer
const uint8_t node_id = 2;              // Tx station node ID: 1-5
uint8_t TxDataInterval = 2;             // Tx every xxxx sec

// pin assignment
const uint8_t LEDpin[4] = { 5,4,3,2 };  // LED pin for LED1, LED2, LED3, LED4
const uint8_t SR04_TRIGpin = 6;
const uint8_t SR04_ECHOpin = 7;

// Threshold
const uint8_t PwrIncThres = 3;          // consecutive error to increase Tx Power (15 sec)
const uint8_t PwrDecThres = 60;         // consecutive success to decrease Tx Power (5min)
const uint8_t PwrBackOffThres = 30;     // consecutive Error at PA_MAX before swtich to PA_MIN (5min)

// ========================================================
struct NodeDataType {
    uint8_t nodeData = node_id; // xxyy zzzz, xx - reserved, yy - Tx Power, zzzz: node Id
    uint8_t pcterror;           // percent error
    uint8_t nextData = TxDataInterval;      // next time data sent, sec
    uint16_t data = 0;          // data to sent
};

struct PowerControlType {
    uint8_t PALevel = 0x00;           // Tx Power (0..4,7) =  MIN, LOW, HIGH, MAX, MIN (back-off), MAX(back-off retry)
    uint8_t ConsErrCnt = 0;           // consecutive Error Tx Counter
    uint8_t ConsSuccCnt = 0;          // consecutive Success Tx Counter
    uint8_t ConsErrBackOffCnt = 0;    // consecutive Error at TA_MAX Tx Counter
} PwrControl;

const uint16_t MAX_DIST = 23200;        // Anything over 400 cm (23200 us pulse) is "out of range"

// Topology
RF24 radio(9,10);    // NRF24L01 SPI config: CE pin9 & CSN pin10
const uint64_t talking_pipes[5] = { 0xF0F0F0F0D2LL, 0xF0F0F0F0C3LL, 0xF0F0F0F0B4LL, 0xF0F0F0F0A5LL, 0xF0F0F0F096LL };
const uint64_t listening_pipes[5] = { 0x3A3A3A3AD2LL, 0x3A3A3A3AC3LL, 0x3A3A3A3AB4LL, 0x3A3A3A3AA5LL, 0x3A3A3A3A96LL };
uint8_t SQN = 1;        // sequence number of next Tx, 1..128

NodeDataType TxData;
uint32_t DataErr[4] = {0,0,0,0};    // DataError bit mask (32 x 4 = 127 bits) 
SimpleTimer timer;

void setup() {
    Serial.begin(57600);
    Init_Peripheral();
    RF24initTx();                                       // Setup and configure RF radio
    timer.setInterval((long)TxDataInterval * 1000, TransmitData);    // Call TransmitData every 5sec
    Serial.println("RF24 - Tx Station");
}

void loop(void) {
    timer.run();
}

void TransmitData(void) {
    uint8_t result;

    UpdateTxPower();                                        // Adjust PA power before sending data
    TxData.pcterror = getBER();                             // fill-in BER value
    TxData.nodeData = node_id;                              // fill-in nodeData with nodeID
    TxData.nodeData |= (PwrControl.PALevel & 0x03) << 4;    // fill-in nodeData with PALevel
    TxData.data = getDistance();                            // fill-in data to be sent out
    result = sendData();
   
    if (result == 0) {                          // sent failed
        Serial.print(" -> Retrying: "); 
        result = sendData();                    // give another try
        if (result == 0) {                      // sent failed again
            TxFailed ();
        } else {
            TxSuccess ();
        }
    } else {                                    // sent success
        TxSuccess ();
        switch (result) {
            case 1: break;                      // success, no CMD
            case 2: break;                      // success, invalid CMD
            case 101: resetBER(); break;        // CMD: 101, reset BER
        }
    }
    SQN++;   // Sequence Number of next Tx, 1..128
    if (SQN > 128) SQN = 1;
}

void TxFailed (void) {
    LEDBar (0);                               // Update LED Status to 0 (turn-off)
    PwrControl.ConsErrCnt++;
    PwrControl.ConsSuccCnt = 0;               // reset Consecutive Success Counter
    switch (PwrControl.PALevel) {
        case 3:                               // if PA is MAX or MIN_Back-Off, increase Back-off counter
        case 4:
            PwrControl.ConsErrBackOffCnt++;
            break;
        case 7:                               // After Tx, check if PA MAX_back-off retry, change to MIN back-off,
            PwrControl.PALevel = 4;
            radio.setPALevel(RF24_PA_MIN);    // Reduce Tx ASAP to save bettery
    }
}

void TxSuccess (void) {
    LEDBar (PwrControl.PALevel + 1);        // Update LED Status of PA power of last Tx
    PwrControl.ConsErrCnt = 0;              // reset Consecutive Error Counter
    PwrControl.ConsErrBackOffCnt = 0;       // reset counter
    PwrControl.ConsSuccCnt++;
    if (PwrControl.PALevel > 3) {           // if PA in Back-off state, change ot MIN to start power control
        PwrControl.PALevel = 0;      
    }
}

// ============================= Command Code Function ===============================
void resetBER(void) {       // CMD 1
    memset(DataErr, 0, sizeof(DataErr));
    Serial.println ("  --> Reset BER to 0");
}

// code stored in the sketch: RF24_Tx_Module.ino
void RF24initTx(void) {
    radio.begin();
    radio.setChannel(121);
    radio.setPALevel(RF24_PA_MIN);      //RF24_PA_MIN, RF24_PA_LOW, RF24_PA_HIGH and RF24_PA_MAX
    if (!radio.setDataRate(RF24_250KBPS)) radio.setDataRate(RF24_1MBPS);
    radio.setAutoAck(1);                // Ensure autoACK is enabled
    radio.enableAckPayload();           // Allow optional ack payloads
    radio.enableDynamicPayloads();
    radio.setRetries(15,15);            // Smallest time between retries, max no. of retries
    radio.setPayloadSize(sizeof(NodeDataType));         // Here we are sending 1-byte payloads to test the call-response speed
    
    radio.openWritingPipe(talking_pipes[node_id - 1]);  // Both radios listen on the same pipes by default, and switch when writing
    radio.openReadingPipe(1,listening_pipes[node_id - 1]);

    radio.startListening();                 // Start listening
}

uint8_t sendData (void) {  //Tx data once, return 0: sent failed, 1-success/no Rx command, 2-success/invalid command, 101..199-success/CMD from Rx
    uint8_t rcvCmd;

    Serial.print("Sending SQN-");
    Serial.print(SQN);
    Serial.print(": Next Tx: ");
    Serial.print(TxData.nextData);
    Serial.print(": %err: ");
    Serial.print(TxData.pcterror);
    Serial.print(", TxPower: ");
    Serial.print(((TxData.nodeData & 0x30) >> 4));
    Serial.print(", data: ");
    Serial.print(TxData.data);

    radio.stopListening();                                  // First, stop listening so we can talk.
    if (radio.write( &TxData, sizeof(NodeDataType))) {      // sent success
        updateBER(true);                                    // Update BER accroding to Tx result
        if (radio.isAckPayloadAvailable()) {                // Get Acknowledge from Rx-Station
            while (radio.available()) radio.read( &rcvCmd, sizeof(uint8_t));
            if ((rcvCmd >=101) && (rcvCmd <= 199)) {        // Received CMD 0, 101..199
                Serial.print(" --> OK. Receive CMD: ");
                Serial.println(rcvCmd);
            } else if (rcvCmd == 0) {                       // NOOP
                Serial.println(" --> OK. CMD: 0");
                rcvCmd = 1;
            } else {
                Serial.print(" --> OK. Unknown CMD: ");
                Serial.println(rcvCmd);
                rcvCmd = 2;
            }
        } else {
            Serial.println(" --> OK. No CMD received.");
            rcvCmd = 1;
        }
    } else {                                                // sent fail
        updateBER(false);                                   // Update BER accroding to Tx result
        rcvCmd = 0;
        Serial.println(" --> err.");
    }
    return rcvCmd;
}

void UpdateTxPower(void) {
    boolean PowerChange = false;
    if (PwrControl.ConsErrCnt >= PwrIncThres) {             // error reach threshold, increase power
        PwrControl.ConsErrCnt = 0;                          // reset counter
        if (PwrControl.PALevel < 3) {                       // if PA already MAX, do nothing
            PwrControl.PALevel++;   // increase power
            PowerChange = true;
        }
    }
    if (PwrControl.ConsErrBackOffCnt >= PwrBackOffThres) {  // error @PA_MAX reach threshold, back-off power
        PwrControl.ConsErrBackOffCnt = 0;                   // reset counter
        if (PwrControl.PALevel == 3) {                      // if PA is MAX
            PwrControl.PALevel = 4;                         // Power Back-Off to MIN
            PowerChange = true;
        } else if (PwrControl.PALevel == 4) {               // if PA is MIN_Back-oof
            PwrControl.PALevel = 7;                         // Power Back-Off to MAX_retry
            PowerChange = true;
        }
    }
    if (PwrControl.ConsSuccCnt >= PwrDecThres) {            // Success Tx reach threshold, decrease power
        PwrControl.ConsSuccCnt = 0;                         // reset counter
        PwrControl.ConsErrCnt = 0;
        if (PwrControl.PALevel > 0) {                       // if PA already MIN, do nothing
            PwrControl.PALevel--;   // decrease power
            PowerChange = true;
        }
    }
    if (PowerChange) {     // Power state changed
        switch (PwrControl.PALevel & 0x03) {
            case 0: radio.setPALevel(RF24_PA_MIN); break;   // PALevel 0,4
            case 1: radio.setPALevel(RF24_PA_LOW); break;   // PALevel 1
            case 2: radio.setPALevel(RF24_PA_HIGH); break;  // PALevel 2
            case 3: radio.setPALevel(RF24_PA_MAX); break;   // PALevel 3,7
        }
    }
}
